// Digital circuit ALU_CU.dig as structural Verilog
module ALU_CU (
  input  BGN,
  input  RST,
  input  CLK
);

  sequnceCNTmod sequncecntmod_1 ();  // open: CLK, BGN, RST, END, Φ0, Φ1, Φ2, Φ3, Φ4, Φ5, Φ6, Φ7
endmodule
